// Logisim project cpu.circ as structural Verilog: 1 circuit, main circuit main
module main (
  input  [31:0] INSTRUCTION,
  input  CLOCK,
  output [31:0] PROGRAM_COUNTER,
  output [31:0] ra,
  output [31:0] sp,
  output [31:0] t0,
  output [31:0] t1,
  output [31:0] t2,
  output [31:0] s0,
  output [31:0] s1,
  output [31:0] a0
);

  wire branch_comp_1_breq, branch_comp_1_brlt, BSel, control_logic_1_brun, RegWEn;
  wire [2:0] ImmSel;
  wire [3:0] control_logic_1_out_10;
  wire [31:0] adder_1_out, ALU_result, imm, inst, multiplexer_1_out, RegFile_read_data_1, RegFile_read_data_2;

  control_logic control_logic_1 (
    .BSel(BSel), .BrUn(control_logic_1_brun), .RegWEn(RegWEn), .ImmSel(ImmSel), .BrLt(branch_comp_1_brlt),
    .BrEq(branch_comp_1_breq), .inst(inst), .out_10(control_logic_1_out_10));  // open: ASel, PCSel, MemRW, WBSel
  Adder #(.width(32)) adder_1 (.a(PROGRAM_COUNTER), .b(32'h4), .out(adder_1_out));  // open: cin, cout
  Register #(.width(32)) PC (.D(adder_1_out), .clk(CLOCK), .Q(PROGRAM_COUNTER));  // open: en, clr
  // Probe on imm
  imm_gen imm_gen_1 (.ImmSel(ImmSel), .inst(INSTRUCTION), .imm(imm));
  // Probe on RegWEn
  // Probe on ImmSel
  regfile_main RegFile (
    .rs2(INSTRUCTION[24:20]), .rd(INSTRUCTION[11:7]), .Read_Data_1(RegFile_read_data_1),
    .Read_Data_2(RegFile_read_data_2), .ra(ra), .sp(sp), .t0(t0), .t1(t1), .t2(t2), .s0(s0), .s1(s1),
    .a0(a0), .rs1(INSTRUCTION[19:15]), .Write_Data(ALU_result), .RegWEn(RegWEn), .clk(CLOCK));
  branch_comp branch_comp_1 (
    .BrEq(branch_comp_1_breq), .BrLt(branch_comp_1_brlt), .BrUn(control_logic_1_brun));  // open: rs1, rs2
  Multiplexer #(.width(32), .enable("false")) multiplexer_1 (
    .in0(RegFile_read_data_2), .in1(imm), .out(multiplexer_1_out), .sel(BSel));
  // Probe on RegFile_read_data_1
  // Probe on multiplexer_1_out
  alu Arithmetic_Logic_Unit (
    .ALUSel(control_logic_1_out_10), .Result(ALU_result), .A(RegFile_read_data_1), .B(multiplexer_1_out));
  // Probe on BSel
  // mem_main DMEM: pin names not known; wires that end beside it: CLOCK

  // Other names for the same wires on the sheet: clk = CLOCK; rd_5[4:0] = INSTRUCTION[11:7];
  //   rs1_5[4:0] = INSTRUCTION[19:15]; rs2_5[4:0] = INSTRUCTION[24:20]

  // Notes on the sheet:
  //   Output
  //   IMEM (do **NOT** move this)
  //   Inputs
  //   It is OK to move the PC, RegFile, ALU, MEM, Branch Comp, Imm Gen, and Control Logic to wherever is most convenient for you when constructing your CPU, and to delete this text
  //   Inputs/Outputs for testing. Do **NOT** move these.
endmodule
