// Logisim project imm_gen.circ as structural Verilog: 3 circuits, main circuit imm_gen
module imm_gen (
  input  [31:0] inst,
  input  [2:0] ImmSel,
  output [31:0] imm
);

  // Probe on imm
  Imm_12_32_extensor imm_12_32_extensor_1 (.instruction(inst), .imm_32_bits(imm));

  // Other names for the same wires on the sheet: opcode[6:0] = inst[6:0]

  // Notes on the sheet:
  //   INPUTS to your circuit
  //   DON'T CHANGE THE LOCATIONS OF THE INPUTS AND OUTPUTS!
  //   OUTPUT from your circuit
endmodule

module Imm_12_32_extensor (
  input  [31:0] instruction,
  output [31:0] imm_32_bits
);

  imm_12_bits imm_12_bits_1 (
    .bit_11(imm_32_bits[31]), .bits_0_11(imm_32_bits[11:0]), .instruction(instruction));  // open: bits_5_11, bits_0_4
  // Probe on {{20{imm_32_bits[31]}}, imm_32_bits[11:0]}

  assign imm_32_bits[30:12] = {19{imm_32_bits[31]}};
endmodule

module imm_12_bits (
  input  [31:0] instruction,
  output [4:0] bits_0_4,
  output [6:0] bits_5_11,
  output [11:0] bits_0_11,
  output bit_11
);


  assign bit_11 = instruction[31];
  assign bits_0_4 = instruction[24:20];
  assign bits_0_11 = instruction[31:20];
  assign bits_5_11 = instruction[31:25];
endmodule
